# Fritzing sketch Master (saved by Fritzing 0.9.3b)
stripboards: 1

parts:
  J1 = female pin header, 8 pins [form="♀ (female)"]
  T1 = LM35 Temperature Sensor [package="TO92 [THT]"]  # not connected
  WeMos_D1_Mini1 = WeMos D1 Mini  # not connected
  J2 = female pin header, 8 pins [form="♀ (female)"]
  U1 = FS1000A - 433Mhz RF Transmitter [package=THT]
  U2 = XD-RF-5V [package=THT]
  J3 = female pin header, 4 pins [form="♀ (female)"]
  S1 = Pushbutton [package="[THT]"]
  S2 = Pushbutton [package="[THT]"]
  J5 = male pin header, 2 pins [form="♂ (male)"]
  J6 = male pin header, 2 pins [form="♂ (male)"]

nets:
  N1: J1.pin4, J3.pin4
  N2: J1.pin5, J3.pin3
  GND: J2.pin1, J2.pin8, U1.GND, U2.GND, J3.pin1, S1.Pin_3, S1.Pin_4, S2.Pin_3, S2.Pin_4, J5.pin1
  N3: J2.pin2, S2.Pin_1, S2.Pin_2
  N4: J2.pin3, S1.Pin_1, S1.Pin_2
  N5: J2.pin4, U2.DATA#2
  N6: J2.pin5, U1.DATA
  N7: J2.pin6, J2.pin7, J6.pin1, J6.pin2
  VCC: U1.VCC, U2.VCC, J3.pin2, J5.pin2

custom parts:
  FS1000A - 433Mhz RF Transmitter: This is 433Mhz RF transmitter with receiver kit for Arduino ARM MCU wireless Application environment: Remote control switch, receiver module, motorcycles, automobile anti-theft products, home security products, electric doors, shutter doors, windows, remote control socket, remote control LED, remote audio remote control electric doors, garage door remote control, remote control retractable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
  XD-RF-5V: This is 433Mhz RF transmitter with receiver kit for Arduino ARM MCU wireless Application environment: Remote control switch, receiver module, motorcycles, automobile anti-theft products, home security products, electric doors, shutter doors, windows, remote control socket, remote control LED, remote audio remote control electric doors, garage door remote control, remote control retractable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
