# Fritzing sketch PumpController (saved by Fritzing 0.9.3b)
stripboards: 1

parts:
  Part1 = Arduino Pro Mini v13
  U1 = FS1000A - 433Mhz RF Transmitter [package=THT]
  U2 = XD-RF-5V [package=THT]
  U3 = TEMPERATURE-SENSOR [package=to-92]
  R1 = Resistor [tolerance=±5% resistance=4.7k package=THT]
  J1 = male pin header, 1 pin [form="♂ (male)"]
  D5/Send = male pin header, 1 pin [form="♂ (male)"]
  D9/Temp = male pin header, 1 pin [form="♂ (male)"]
  J6 = male pin header, 1 pin [form="♂ (male)"]
  D3/Relais = male pin header, 1 pin [form="♂ (male)"]
  D2/Receive = male pin header, 1 pin [form="♂ (male)"]
  J9 = male pin header, 1 pin [form="♂ (male)"]
  U4 = mystery part, 3 pins [chip_label=Relais]

nets:
  GND: Part1.GND, Part1.D7, U1.GND, U2.GND, U3.GND, J6.pin1, U4.pin2
  N1: Part1.RESET, Part1.D2, U2.DATA, D2/Receive.pin1
  VCC: Part1.VCC, Part1.D10_PWM/SS, Part1.D6_PWM, Part1.D0/TX, U1.VCC, U2.VCC, U3.VCC, R1.Pin_0, J1.pin1, U4.pin3
  N2: Part1.D11_PWM/MOSI, J9.pin1
  N3: Part1.D9_PWM, U3.ADJ, R1.Pin_1, D9/Temp.pin1
  N4: Part1.D5_PWM, U1.DATA, D5/Send.pin1
  N5: Part1.D3_PWM, D3/Relais.pin1, U4.pin1

custom parts:
  FS1000A - 433Mhz RF Transmitter: This is 433Mhz RF transmitter with receiver kit for Arduino ARM MCU wireless Application environment: Remote control switch, receiver module, motorcycles, automobile anti-theft products, home security products, electric doors, shutter doors, windows, remote control socket, remote control LED, remote audio remote control electric doors, garage door remote control, remote control retractable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
  XD-RF-5V: This is 433Mhz RF transmitter with receiver kit for Arduino ARM MCU wireless Application environment: Remote control switch, receiver module, motorcycles, automobile anti-theft products, home security products, electric doors, shutter doors, windows, remote control socket, remote control LED, remote audio remote control electric doors, garage door remote control, remote control retractable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
